# Fritzing sketch esp32_step_6a (saved by Fritzing 0.9.5d)
breadboards: 1

parts:
  LED2 = LED - 5mm [color="Red (633nm)" package="5 mm [THT]"]
  R3 = Resistor [tolerance=±5% resistance=220 package="1206 [SMD]"]

nets:
  N1: LED2.anode, R3.Pin_0
