# Fritzing sketch esp32_step_8 (saved by Fritzing 0.9.5d)
breadboards: 1

parts:
  LED2 = LED - 5mm [color="Red (633nm)" package="5 mm [THT]"]
  R3 = Resistor [tolerance=±5% resistance=220 package="1206 [SMD]"]
  U2 = LuaNode32 / ESP32 [part_number=ESP32S-PIN30]
  T3 = TMP36 Temperature Sensor [package="TO92 [THT]"]  # not connected
  T4 = TMP36 Temperature Sensor [package="TO92 [THT]"]

nets:
  GND: LED2.cathode, U2.GND, T4.GND
  N1: LED2.anode, R3.Pin_0
  N2: R3.Pin_1, U2.D32
  N3: U2.D34, T4.Vout
  N4: U2.3V3, T4.+Vs

custom parts:
  LuaNode32 / ESP32: New Image for LuaNode32 DOIT ESP32 DEVKIT V1. Base parts from LuaNode32 / ESP32 ESP32 based LuaNode32 by G.Noorlander DOIT Esp32 DevKit v1 (30 pins long, 11 pins width) by Werner Rothschopf (modified by vanepp Dec 2018)
